# Fritzing sketch practica1 (saved by Fritzing 0.9.3b)
breadboards: 1

parts:
  R1 = Rotary Potentiometer (Small) [maximum_resistance=100kΩ package=THT]
  74HC139N1 = 74HC139N [part_number=74HC08 package="DIP (Dual Inline) [THT]"]
  Power_plug1 = Power plug

nets:
  N1: R1.leg1, 74HC139N1.1G_, Power_plug1.VCC
  N2: R1.wiper, 74HC139N1.1A
  GND: R1.leg2, 74HC139N1.GND, Power_plug1.GND

notes:
  Osciloscopio
  *el código del chip no es el de la practica
