# Fritzing sketch reloj (saved by Fritzing 0.9.3b)
breadboards: 1

parts:
  74HC139N1 = 74HC139N [part_number=74HC08 package="DIP (Dual Inline) [THT]"]
  Power_plug1 = Power plug
  LED1 = LED - 5mm [color="Red (633nm)" package="5 mm [THT]"]  # not connected

nets:
  GND: 74HC139N1.GND, Power_plug1.GND

notes:
  Osciloscopio
  *el código del chip no es el de la practica
  interruptor
  reloj (1Hz - 1KHz)
